# Fritzing sketch DCCInspectorShield (saved by Fritzing 1.0.4)
circuit board: 8.46667cm x 5.64444cm

parts:
  R3 = Resistor [tolerance=±5% power=0.25W resistance=2.2k package=THT]
  D1 = Rectifier Diode [part_number=1N4001 package="300 mil [THT]"]
  C1 = Ceramic Capacitor [capacitance=100nF voltage=35V package="100 mil [THT, multilayer]"]
  R1 = Resistor [tolerance=±5% power=0.25W resistance=470 package=THT]
  R2 = Resistor [tolerance=±5% power=0.25W resistance=1.5k package=THT]
  R4 = Resistor [tolerance=±5% power=0.25W resistance=1k package=THT]
  R5 = Resistor [tolerance=±5% power=0.25W resistance=330 package=THT]
  IC1 = IC, DIP package, 8 pins [chip_label=IC]
  J2 = Camdenboss CTB0158-3 [part_number=CTB0158-3 package=THT]
  J1 = Camdenboss CTB0158-2 [part_number=CTB0158-2 package=THT]
  Part5 = Arduino Prototyping Shield

nets (from the breadboard view):
  N1: R3.Pin_0, J2.pin1, Part5.N$427, Part5.N$428
  N2: R3.Pin_1, D1.cathode, C1.1, R2.Pin_1, R4.Pin_1, R5.Pin_1, Part5.N$299, Part5.N$305, Part5.N$310, Part5.N$317, Part5.N$358, Part5.N$365, Part5.N$413, Part5.N$432
  N3: D1.anode, C1.0, IC1.pin3, J1.pin2, Part5.N$263, Part5.N$316, Part5.N$327, Part5.N$354, Part5.N$357, Part5.N$368, Part5.N$377
  N4: R1.Pin_0, IC1.pin8, Part5.N$229, Part5.N$236
  N5: R1.Pin_1, IC1.pin6, Part5.D8, Part5.N$241, Part5.N$268, Part5.N$435
  N6: R2.Pin_0, J2.pin2, Part5.N$405, Part5.N$406
  N7: R4.Pin_0, J2.pin3, Part5.N$398, Part5.N$399
  N8: R5.Pin_0, J1.pin1, Part5.N$93, Part5.N$380
  N9: IC1.pin1, Part5.N$261
  N10: IC1.pin2, Part5.N$262
  N11: IC1.pin4, Part5.N$298
  N12: IC1.pin5, Part5.GND, Part5.N$203, Part5.N$267, Part5.N$416, Part5.N$417
  N13: IC1.pin7, Part5.N$239
  N14: Part5.+5V, Part5.N$251, Part5.N$360
  N15: Part5.N$281, Part5.N$295
